# Fritzing sketch Car (saved by Fritzing 0.9.3b)

parts:
  S1 = H-Bridge with L298N
  Часть1 = Arduino Nano (Rev3.0)
  M1 = DC Motor
  M2 = DC Motor
  Часть2 = Bluetooth HC-05 Macho
  part = Resistor [tolerance=±5% resistance=220 package=THT]
  R2 = Resistor [tolerance=±5% resistance=220 package=THT]
  hc-sr1 = hc-sr04
  LED1 = LED - 5mm [color="White (4500K)" package="5 mm [THT]"]
  LED2 = LED - 5mm [color="White (4500K)" package="5 mm [THT]"]

nets:
  5V: S1.12V, S1.5V, Часть1.5V, Часть2.VCC, hc-sr1.VCC
  GND: S1.GND, Часть1.GND, Часть2.GND, hc-sr1.GND, LED1.cathode, LED2.cathode
  N1: S1.ENA, S1.ENA-5V
  N2: S1.IN1, Часть1.D2
  N3: S1.IN2, Часть1.D3
  N4: S1.IN3, Часть1.D5
  N5: S1.IN4, Часть1.D6
  N6: S1.ENB, S1.ENB-5V
  N7: S1.M1-01, M2.pin_2
  N8: S1.M1-02, M2.pin_1
  N9: S1.M2-01, M1.pin_2
  N10: S1.M2-02, M1.pin_1
  N11: Часть1.D1/TX, Часть2.RXD
  N12: Часть1.D0/RX, Часть2.TXD
  N13: Часть1.D8, R2.Pin_1
  N14: Часть1.D9, part.Pin_1
  N15: Часть1.D11/MOSI, hc-sr1.Trig
  N16: Часть1.D12/MISO, hc-sr1.Echo

custom parts:
  H-Bridge with L298N: h-bridge
